# Fritzing sketch GENAS Hardware Diagram straight (saved by Fritzing 0.9.3b)
circuit board: 8.67914cm x 5.78103cm
breadboards: 2

parts:
  Raspberry_Pi_1 = Raspberry Pi 3 [part_number=RPI-3-V1.2]
  LED1 = LED - 5mm [color="Red (633nm)" package="5 mm [THT]"]  # not connected
  LED2 = LED - 5mm [color="Green (560nm)" package="5 mm [THT]"]  # not connected
  LED3 = LED - 5mm [color="Yellow (595nm)" package="5 mm [THT]"]  # not connected
  DS1 = DS18B20 1-Wire Temperature Sensor [part_number=DS18B20]
  R1 = Resistor [tolerance=±5% resistance=4.7k package=THT]
  Part1 = Adafruit TCS34725 RGB Color Sensor [part_number="Adafruit #1334"]
  Blue_light_emitter = LED - 5mm [color="Blue (470nm)" package="5 mm [THT]"]
  R2 = Resistor [tolerance=±5% resistance=220 package=THT]
  MIC1 = Microphone  # not connected
  SP1 = SPEAKER [package=pcb_mount_speaker]  # not connected
  U1 = LCD-16X2 [package=lcd-16x2]
  R3 = Trimmer Potentiometer [maximum_resistance=10kΩ package=THT]
  Part2 = Adafruit TSL2561 [part_number="Adafruit #439"]

nets (from the breadboard view):
  3V3: Raspberry_Pi_1.3v3, Raspberry_Pi_1.3V3, Part1.VIN, Part2.VIN
  N1: Raspberry_Pi_1.GPIO2, Part1.SDA, Part2.SDA
  N2: Raspberry_Pi_1.GPIO3, Part1.SCL, Part2.SCL
  N3: Raspberry_Pi_1.GPIO4, DS1.DQ, R1.Pin_0
  GND: Raspberry_Pi_1.GND, DS1.GND, Part1.GND, R2.Pin_1, U1.VSS, U1.R_W, U1.K, R3.leg1, Part2.GND
  N4: Raspberry_Pi_1.GPIO26, Blue_light_emitter.cathode
  N5: Raspberry_Pi_1.GPIO7, U1.RS
  N6: Raspberry_Pi_1.GPIO8, U1.E
  N7: Raspberry_Pi_1.GPIO25, U1.DB4
  N8: Raspberry_Pi_1.GPIO24, U1.DB5
  N9: Raspberry_Pi_1.GPIO23, U1.DB6
  N10: Raspberry_Pi_1.GPIO18, U1.DB7
  VDD: Raspberry_Pi_1.5V, DS1.VDD, R1.Pin_1, U1.VDD, U1.A, R3.leg2
  N11: Blue_light_emitter.anode, R2.Pin_0
  N12: U1.VO, R3.wiper

custom parts:
  Adafruit TCS34725 RGB Color Sensor: Your electronics can now see in dazzling color with this lovely color light sensor. We found the best color sensor on the market, the TCS34725, which has RGB and Clear light sensing elements. An IR blocking filter, integrated on-chip and localized to the color sensing photodiodes, minimizes the IR spectral component of the incoming light and allows color measurements to be made accurately. The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
  Adafruit TSL2561: The TSL2561 luminosity sensor is an advanced digital light sensor, ideal for use in a wide range of light situations. Compared to low cost CdS cells, this sensor is more precise, allowing for exact lux calculations and can be configured for different gain/timing ranges to detect light ranges from up to 0.1 - 40,000+ Lux on the fly. The best part of this sensor is that it contains both infrared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
